# Fritzing sketch LV22-Vend-A-Python (saved by Fritzing 0.9.1b)

parts:
  X1 = X113647 Stepper Driver Board [package=board]
  Raspberry_Pi1 = Raspberry Pi B+
  S2 = Momentary Switch [package=ksa_sealed_tac_switch]

nets:
  N1: X1.IN1, Raspberry_Pi1.GPIO17
  N2: X1.IN2, Raspberry_Pi1.GPIO10
  N3: X1.IN3, Raspberry_Pi1.GPIO9
  N4: X1.IN4, Raspberry_Pi1.GPIO11
  GND: X1.GND, Raspberry_Pi1.GND, S2.3
  N5: X1.+V, Raspberry_Pi1.5V
  N6: Raspberry_Pi1.GPIO23, S2.1

custom parts:
  X113647 Stepper Driver Board: A common stepper motor driver board based on ULN2003APG darlington array
